# Fritzing sketch PowerRail_Rev2 (saved by Fritzing 1.0.2b)
circuit board: 9.9cm x 5.33cm

parts:
  J1 = female pin header, 8 pins [form="♀ (female)"]
  J2 = female pin header, 8 pins [form="♀ (female)"]
  J3 = female pin header, 8 pins [form="♀ (female)"]
  J4 = female pin header, 8 pins [form="♀ (female)"]
  J5 = female pin header, 8 pins [form="♀ (female)"]
  J6 = female pin header, 8 pins [form="♀ (female)"]
  J7 = female pin header, 8 pins [form="♀ (female)"]
  J8 = female pin header, 8 pins [form="♀ (female)"]
  J9 = female pin header, 8 pins [form="♀ (female)"]
  J10 = female pin header, 8 pins [form="♀ (female)"]
  JA = screw terminal, 3 pins
  JB = screw terminal, 3 pins
  C3 = Ceramic Capacitor [capacitance=100nF voltage=35V package="100 mil [THT, multilayer]"]
  C2 = Ceramic Capacitor [capacitance=100nF voltage=35V package="100 mil [THT, multilayer]"]
  C1 = Ceramic Capacitor [capacitance=100nF voltage=35V package="100 mil [THT, multilayer]"]
  D1 = Rectifier Diode [part_number=1N4007 package="300 mil [THT]"]
  C5 = Tantalum Capacitor [capacitance=1μF package="100 mil [THT, tantalum]"]
  D2 = Rectifier Diode [part_number=1N4007 package="300 mil [THT]"]
  C4 = Tantalum Capacitor [capacitance=1μF package="100 mil [THT, tantalum]"]
  7805 = Voltage Regulator [part_number=7805 package=to-220-alt]
  JB1 = screw terminal, 3 pins
  JA1 = screw terminal, 3 pins
  J11 = female pin header, 8 pins [form="♀ (female)"]
  J12 = female pin header, 8 pins [form="♀ (female)"]
  J13 = female pin header, 8 pins [form="♀ (female)"]
  J14 = female pin header, 8 pins [form="♀ (female)"]
  J15 = female pin header, 8 pins [form="♀ (female)"]
  J16 = female pin header, 8 pins [form="♀ (female)"]
  C6 = Electrolytic Capacitor [capacitance=10µF package="100 mil [THT, electrolytic]"]
  C7 = Electrolytic Capacitor [capacitance=10µF voltage=35V package="100 mil [THT, electrolytic]"]
  C8 = Electrolytic Capacitor [capacitance=10µF package="100 mil [THT, electrolytic]"]
  12V = LED - 3mm [color="Red (633nm)" current=0.030A package="3 mm [THT]"]
  -12V = LED - 3mm [color="Red (633nm)" current=0.030A package="3 mm [THT]"]
  5V = LED - 3mm [color="Red (633nm)" current=0.030A package="3 mm [THT]"]
  R1 = Resistor [tolerance=±5% resistance=1k power=0.25W package=THT]
  R2 = Resistor [tolerance=±5% resistance=1k power=0.25W package=THT]
  R3 = Resistor [tolerance=±5% resistance=1k power=0.25W package=THT]
  H1 = male pin header, 3 pins [form="♂ (male)"]
  H2 = male pin header, 3 pins [form="♂ (male)"]
  H3 = male pin header, 3 pins [form="♂ (male)"]
  H4 = male pin header, 3 pins [form="♂ (male)"]

nets:
  gate: J1.pin1, J2.pin1, J3.pin1, J4.pin1, J5.pin1, J6.pin1, J7.pin1, J8.pin1, J9.pin1, J10.pin1, J11.pin1, J12.pin1, J13.pin1, J14.pin1, J15.pin1, J16.pin1
  CV: J1.pin2, J2.pin2, J3.pin2, J4.pin2, J5.pin2, J6.pin2, J7.pin2, J8.pin2, J9.pin2, J10.pin2, J11.pin2, J12.pin2, J13.pin2, J14.pin2, J15.pin2, J16.pin2
  5V: J1.pin3, J2.pin3, J3.pin3, J4.pin3, J5.pin3, J6.pin3, J7.pin3, J8.pin3, J9.pin3, J10.pin3, C3.1, D1.anode, C5.+, D2.cathode, 7805.OUT, J11.pin3, J12.pin3, J13.pin3, J14.pin3, J15.pin3, J16.pin3, C8.+, R3.Pin_0
  12V: J1.pin4, J2.pin4, J3.pin4, J4.pin4, J5.pin4, J6.pin4, J7.pin4, J8.pin4, J9.pin4, J10.pin4, JA.pin1, JB.pin3, C1.0, D1.cathode, C4.+, 7805.IN, JB1.pin3, JA1.pin1, J11.pin4, J12.pin4, J13.pin4, J14.pin4, J15.pin4, J16.pin4, C6.+, R1.Pin_0, H1.pin1, H2.pin1, H3.pin1, H4.pin1
  GND: J1.pin5, J1.pin6, J1.pin7, J2.pin5, J2.pin6, J2.pin7, J3.pin5, J3.pin6, J3.pin7, J4.pin5, J4.pin6, J4.pin7, J5.pin5, J5.pin6, J5.pin7, J6.pin5, J6.pin6, J6.pin7, J7.pin5, J7.pin6, J7.pin7, J8.pin5, J8.pin6, J8.pin7, J9.pin5, J9.pin6, J9.pin7, J10.pin5, J10.pin6, J10.pin7, JA.pin2, JB.pin2, C3.0, C2.0, C1.1, C5.-, D2.anode, C4.-, 7805.GND, JB1.pin2, JA1.pin2, J11.pin5, J11.pin6, J11.pin7, J12.pin5, J12.pin6, J12.pin7, J13.pin5, J13.pin6, J13.pin7, J14.pin5, J14.pin6, J14.pin7, J15.pin5, J15.pin6, J15.pin7, J16.pin5, J16.pin6, J16.pin7, C6.-, C7.+, C8.-, 12V.cathode, -12V.anode, 5V.cathode, H1.pin2, H2.pin2, H3.pin2, H4.pin2
  -12V: J1.pin8, J2.pin8, J3.pin8, J4.pin8, J5.pin8, J6.pin8, J7.pin8, J8.pin8, J9.pin8, J10.pin8, JA.pin3, JB.pin1, C2.1, JB1.pin1, JA1.pin3, J11.pin8, J12.pin8, J13.pin8, J14.pin8, J15.pin8, J16.pin8, C7.-, R2.Pin_0, H1.pin3, H2.pin3, H3.pin3, H4.pin3
  N1: 12V.anode, R1.Pin_1
  N2: -12V.cathode, R2.Pin_1
  N3: 5V.anode, R3.Pin_1

notes:
  gate
  cv
  5V
  12V
  Power Rails
  Rev 2.1
  GND
  -
  Designed by drChungus
